# Fritzing sketch portail_na_1 (saved by Fritzing 0.9.9b)
circuit board: 8.46667cm x 5.64444cm
breadboards: 1

parts:
  LCD2 = LCD screen [part_number=1602A]
  R6 = Resistor [tolerance=±5% resistance=1k package="2010 [SMD]"]
  J4 = screw terminal, 2 pins [part_number=TRIG]
  R7 = Resistor [tolerance=±5% resistance=1k package="2010 [SMD]"]
  Composant2 = Arduino Nano (Rev3.0)
  J5 = Screw terminal - 2 pins [part_number=ALIM12V package=THT]
  J6 = Screw terminal - 2 pins [part_number=COUNTROT package=THT]
  R8 = Resistor [tolerance=±5% resistance=1k package="2010 [SMD]"]
  R9 = Resistor [tolerance=±5% resistance=680 package="2010 [SMD]"]
  C10 = Electrolytic Capacitor [capacitance=0.1mF voltage=35V package="1010 [SMD, electrolytic]"]
  R10 = Resistor [tolerance=±5% resistance=100k package="2010 [SMD]"]
  C11 = Electrolytic Capacitor [capacitance=4.7µF voltage=35V package="1010 [SMD, electrolytic]"]
  C12 = Ceramic Capacitor [capacitance=0.22mF voltage=35V package="0805 [SMD, multilayer]"]
  C13 = Ceramic Capacitor [capacitance="100 nF" voltage=35V package="0805 [SMD, multilayer]"]
  U6 = L200 [package="pentawatt h"]
  LCM1602_IIC2 = LCM1602 IIC [part_number="LCM1602 IIC" chip_label="LCM1602 IIC" package="DIP (Dual Inline) [THT]"]
  M2 = DC Motor
  C15 = Electrolytic Capacitor [capacitance=0.1mF voltage=35V package="1010 [SMD, electrolytic]"]
  S2 = H-Bridge with L298N [part_number=ln298]

nets:
  VSS: LCD2.VSS, LCM1602_IIC2.VSS
  VDD: LCD2.VDD, LCM1602_IIC2.VDD
  N1: LCD2.V0, LCM1602_IIC2.V0
  N2: LCD2.RS, LCM1602_IIC2.RS
  N3: LCD2.R/W, LCM1602_IIC2.RW
  N4: LCD2.E, LCM1602_IIC2.E
  N5: LCD2.DB0, LCM1602_IIC2.D0
  N6: LCD2.DB1, LCM1602_IIC2.D1
  N7: LCD2.DB2, LCM1602_IIC2.D2
  N8: LCD2.DB3, LCM1602_IIC2.D3
  N9: LCD2.DB4, LCM1602_IIC2.D4
  N10: LCD2.DB5, LCM1602_IIC2.D5
  N11: LCD2.DB6, LCM1602_IIC2.D6
  N12: LCD2.DB7, LCM1602_IIC2.D7
  N13: LCD2.LED+, LCM1602_IIC2.A
  N14: LCD2.LED-, LCM1602_IIC2.K
  5V: R6.Pin_0, R7.Pin_0, Composant2.5V, LCM1602_IIC2.VCC, C15.+
  N15: R6.Pin_1, J4.pin2, Composant2.D3
  GND: J4.pin1, Composant2.GND, J5.pin1, J6.pin1, R9.Pin_1, C10.-, C11.-, C12.0, C13.1, LCM1602_IIC2.GND, C15.-, S2.GND
  N16: R7.Pin_1, Composant2.D2, J6.pin2
  N17: Composant2.D5, S2.ENA, S2.ENB
  N18: Composant2.D6, S2.IN1, S2.IN3
  N19: Composant2.D7, S2.IN2, S2.IN4
  N20: Composant2.VIN, J5.pin2, C10.+, C12.1
  N21: Composant2.A7, R10.Pin_0
  N22: Composant2.A5, LCM1602_IIC2.SCL
  N23: Composant2.A4, LCM1602_IIC2.SDA
  N24: R8.Pin_0, C13.0, U6.OUTPUT, S2.12V
  N25: R8.Pin_1, R9.Pin_0, R10.Pin_1, C11.+
  N26: LCM1602_IIC2.LED_A, LCM1602_IIC2.LED_B
  N27: M2.pin_1, S2.M1-02, S2.M2-01
  N28: M2.pin_2, S2.M1-01, S2.M2-02

custom parts:
  L200: ADJUSTABLE VOLTAGE AND CURRENT REGULATOR
  LCM1602 IIC: I2C-Module to use a 1602 or 2004 LCD on with the wire.h libory Serial LCD Modul
  H-Bridge with L298N: h-bridge
